// Logisim project RSC.circ as structural Verilog: 9 circuits, main circuit RSC
module RSC (
  output [7:0] T,
  output [3:0] D
);

  wire control_1_acc_bus, control_1_acc_clr, control_1_acc_ld, control_1_ar_ld, control_1_dr_bus,
       control_1_dr_ld, control_1_ir_ld, control_1_outr_ld, control_1_pc_bus, control_1_pc_inc,
       control_1_pc_ld, control_1_r_bus, control_1_r_ld, control_1_ram_en, control_1_ram_r_prime_w,
       control_1_z_ld, Primary_Clock_out, z_reg_1_z_out;
  wire [2:0] control_1_alu_s;
  wire [3:0] outr_1_data_out_2, outr_1_data_out_3, outr_1_data_out_4, outr_1_data_out_5, outr_1_data_out_6;
  wire [11:0] outr_1_data_out;
  wire [31:0] acc_1_data_out, alu_1_alu_out, ar_1_data_out, dr_1_data_out, ir_1_data_out, pc_1_data_out,
       r_1_bus_out, r_1_data_out;

  Clock Primary_Clock (.out(Primary_Clock_out));
  Hex_Digit_Display hex_digit_display_1 (.value(outr_1_data_out_6));  // open: dp
  Hex_Digit_Display hex_digit_display_2 (.value(outr_1_data_out_5));  // open: dp
  AR ar_1 (.Data_In(r_1_bus_out), .Clock(Primary_Clock_out), .Load(control_1_ar_ld), .Data_Out(ar_1_data_out));
  R r_1 (
    .Data_In(r_1_bus_out), .Clock(Primary_Clock_out), .Load(control_1_r_ld), .Bus(control_1_r_bus),
    .Data_Out(r_1_data_out), .Bus_Out(r_1_bus_out));
  Hex_Digit_Display hex_digit_display_3 (.value(outr_1_data_out_4));  // open: dp
  Hex_Digit_Display hex_digit_display_4 (.value(outr_1_data_out_3));  // open: dp
  DR dr_1 (
    .Data_In(r_1_bus_out), .Clock(Primary_Clock_out), .Load(control_1_dr_ld), .Bus(control_1_dr_bus),
    .Data_Out(dr_1_data_out), .Bus_Out(r_1_bus_out));
  OUTR outr_1 (
    .Data_In(r_1_bus_out), .Clock(Primary_Clock_out), .Load(control_1_outr_ld),
    .Data_Out({outr_1_data_out_6, outr_1_data_out_5, outr_1_data_out_4, outr_1_data_out_3, outr_1_data_out_2, outr_1_data_out}));
  Hex_Digit_Display hex_digit_display_5 (.value(outr_1_data_out[11:8]));  // open: dp
  Hex_Digit_Display hex_digit_display_6 (.value(outr_1_data_out_2));  // open: dp
  RAM #(.addrWidth(16), .dataWidth(32)) ram_1 (
    .addr(ar_1_data_out[15:0]), .data(r_1_bus_out), .sel(control_1_ram_en), .clk(Primary_Clock_out),
    .ld(control_1_ram_r_prime_w));  // open: clr
  PC pc_1 (
    .Data_In(r_1_bus_out), .Clock(Primary_Clock_out), .Count(control_1_pc_inc), .Load(control_1_pc_ld),
    .Bus(control_1_pc_bus), .Data_Out(pc_1_data_out), .Bus_Out(r_1_bus_out));
  ACC acc_1 (
    .Data_In(alu_1_alu_out), .Clock(Primary_Clock_out), .Load(control_1_acc_ld), .Clear(control_1_acc_clr),
    .Bus(control_1_acc_bus), .Data_Out(acc_1_data_out), .Bus_Out(r_1_bus_out));
  ALU alu_1 (
    .A(acc_1_data_out), .B(r_1_bus_out), .S2(control_1_alu_s[2]), .S1(control_1_alu_s[1]),
    .S0(control_1_alu_s[0]), .ALU_Out(alu_1_alu_out));
  Hex_Digit_Display hex_digit_display_7 (.value(outr_1_data_out[7:4]));  // open: dp
  Hex_Digit_Display hex_digit_display_8 (.value(outr_1_data_out[3:0]));  // open: dp
  IR ir_1 (.Data_In(dr_1_data_out), .Clock(Primary_Clock_out), .Load(control_1_ir_ld), .Data_Out(ir_1_data_out));
  Control control_1 (
    .RAM_R_prime_W(control_1_ram_r_prime_w), .RAM_EN(control_1_ram_en), .AR_LD(control_1_ar_ld),
    .PC_BUS(control_1_pc_bus), .PC_INC(control_1_pc_inc), .PC_LD(control_1_pc_ld), .DR_BUS(control_1_dr_bus),
    .DR_LD(control_1_dr_ld), .R_BUS(control_1_r_bus), .R_LD(control_1_r_ld), .ACC_BUS(control_1_acc_bus),
    .ACC_CLR(control_1_acc_clr), .ACC_LD(control_1_acc_ld), .ALU_S(control_1_alu_s),
    .OUTR_LD(control_1_outr_ld), .Z_LD(control_1_z_ld), .IR_LD(control_1_ir_ld), .Clock(Primary_Clock_out),
    .Z_In(z_reg_1_z_out), .T(T), .IR_In(ir_1_data_out), .D(D));
  Z_reg z_reg_1 (.ACC_in(acc_1_data_out), .Clock(Primary_Clock_out), .Load(control_1_z_ld), .Z_out(z_reg_1_z_out));
  // Probe on z_reg_1_z_out
  // Probe on pc_1_data_out
  // Probe on dr_1_data_out
  // Probe on ir_1_data_out
  // Probe on r_1_data_out
  // Probe on acc_1_data_out
endmodule

module ALU (
  input  [31:0] A,
  input  [31:0] B,
  input  S2,
  input  S1,
  input  S0,
  output [31:0] ALU_Out
);

  wire [31:0] arith_u_1_au_out, logic_u_1_logic_out;

  Arith_U arith_u_1 (.A(A), .B(B), .S1(S1), .S0(S0), .AU_out(arith_u_1_au_out));
  Logic_U logic_u_1 (.A(A), .B(B), .S1(S1), .S0(S0), .Logic_Out(logic_u_1_logic_out));
  Multiplexer #(.width(32), .enable("false")) multiplexer_1 (
    .in0(arith_u_1_au_out), .in1(logic_u_1_logic_out), .out(ALU_Out), .sel(S2));

  // Notes on the sheet:
  //   Ryan Hines
  //   CLA6
  //   ALU
endmodule

// LU
module Logic_U (
  input  [31:0] A,
  input  [31:0] B,
  input  S1,
  input  S0,
  output [31:0] Logic_Out
);

  wire [31:0] and_1_out, not_1_out, or_1_out, shifter_1_out;

  assign and_1_out = A & B;  // AND_Gate and_1, 32 bits wide
  assign or_1_out = A | B;  // OR_Gate or_1, 32 bits wide
  Shifter #(.width(32), .shift("ar")) shifter_1 (.in(A), .\dist (5'b00001), .out(shifter_1_out));
  Multiplexer #(.select(2), .width(32), .enable("false")) multiplexer_1 (
    .in0(and_1_out), .in1(or_1_out), .in2(shifter_1_out), .in3(not_1_out), .out(Logic_Out), .sel({S1, S0}));
  assign not_1_out = ~A;  // NOT_Gate not_1, 32 bits wide
endmodule

// AU
module Arith_U (
  input  [31:0] A,
  input  [31:0] B,
  input  S1,
  input  S0,
  output [31:0] AU_out
);

  wire and_1_out, not_2_out;
  wire [31:0] adder_1_out, multiplexer_1_out, not_1_out;

  assign not_1_out = ~B;  // NOT_Gate not_1, 32 bits wide
  not not_2 (not_2_out, S0);
  Multiplexer #(.select(2), .width(32), .enable("false")) multiplexer_1 (
    .in0(not_1_out), .in1(B), .in2({32{1'b0}}), .in3(B), .out(multiplexer_1_out), .sel({S1, S0}));
  and and_1 (and_1_out, S1, S0);
  Adder #(.width(32)) adder_1 (.a(A), .b(multiplexer_1_out), .out(adder_1_out), .cin(not_2_out));  // open: cout
  Multiplexer #(.width(32), .enable("false")) multiplexer_2 (
    .in0(adder_1_out), .in1(multiplexer_1_out), .out(AU_out), .sel(and_1_out));

  // Notes on the sheet:
  //   Ryan Hines
  //   CLA4
  //   ALU
endmodule

module SC (
  input  Clock,
  input  Clear,
  output [2:0] SEQ_Out
);

  wire [2:0] adder_1_out;

  Register #(.width(3)) register_1 (.D(adder_1_out), .Q(SEQ_Out), .clk(Clock), .clr(Clear));  // open: en
  Adder #(.width(3)) adder_1 (.a(SEQ_Out), .b(3'b001), .out(adder_1_out));  // open: cin, cout

  // Notes on the sheet:
  //   Ryan Hines
  //   CL7
  //   SC Counter
endmodule

// D
module Decoder (
  input  [31:0] IR_In,
  output [15:0] D_Out,
  output [3:0] Debug_Instruction
);

  wire or_1_out;
  wire [3:0] or_2_out;
  wire [15:0] decoder_1_out0;

  Multiplexer #(.width(16), .enable("false")) multiplexer_1 (
    .in0(decoder_1_out0), .in1({16{1'b0}}), .out(D_Out), .sel(or_1_out));
  Decoder_part #(.select(4), .enable("false")) decoder_1 (
    .out0(decoder_1_out0[0]), .out1(decoder_1_out0[1]), .out2(decoder_1_out0[2]), .out3(decoder_1_out0[3]),
    .out4(decoder_1_out0[4]), .out5(decoder_1_out0[5]), .out6(decoder_1_out0[6]), .out7(decoder_1_out0[7]),
    .out8(decoder_1_out0[8]), .out9(decoder_1_out0[9]), .out10(decoder_1_out0[10]),
    .out11(decoder_1_out0[11]), .out12(decoder_1_out0[12]), .out13(decoder_1_out0[13]),
    .out14(decoder_1_out0[14]), .out15(decoder_1_out0[15]), .sel(IR_In[3:0]));
  or or_1 (or_1_out, or_2_out[0], or_2_out[1], or_2_out[2], or_2_out[3]);
  assign or_2_out = IR_In[7:4] | IR_In[11:8] | IR_In[15:12] | IR_In[19:16] | IR_In[23:20] | IR_In[27:24] | IR_In[31:28];  // OR_Gate or_2, 4 bits wide

  assign Debug_Instruction = IR_In[3:0];
endmodule

// T
module Timer (
  input  Clock,
  input  Stop,
  input  Clear,
  output [7:0] T_Out
);

  wire [2:0] sc_1_seq_out;
  wire [7:0] decoder_1_out0;

  Multiplexer #(.width(8), .enable("false")) multiplexer_1 (
    .in0(decoder_1_out0), .in1({8{1'b0}}), .out(T_Out), .sel(Stop));
  Decoder_part #(.select(3), .enable("false")) decoder_1 (
    .out0(decoder_1_out0[0]), .out1(decoder_1_out0[1]), .out2(decoder_1_out0[2]), .out3(decoder_1_out0[3]),
    .out4(decoder_1_out0[4]), .out5(decoder_1_out0[5]), .out6(decoder_1_out0[6]), .out7(decoder_1_out0[7]),
    .sel(sc_1_seq_out));
  SC sc_1 (.Clear(Clear), .Clock(Clock), .SEQ_Out(sc_1_seq_out));
endmodule

// Z
module Z_reg (
  input  Clock,
  input  Load,
  input  [31:0] ACC_in,
  output Z_out
);

  wire multiplexer_1_out, or_2_out;
  wire [3:0] or_1_out;

  assign or_1_out = ACC_in[3:0] | ACC_in[7:4] | ACC_in[11:8] | ACC_in[15:12] | ACC_in[19:16] | ACC_in[23:20] | ACC_in[27:24] | ACC_in[31:28];  // OR_Gate or_1, 4 bits wide
  or or_2 (or_2_out, or_1_out[0], or_1_out[1], or_1_out[2], or_1_out[3]);
  _1bit_reg u_1bit_reg_1 (.Data(multiplexer_1_out), .Clock(Clock), .Load(Load), .Data_out(Z_out));  // open: Clear
  Multiplexer #(.enable("false")) multiplexer_1 (.in0(1'b1), .in1(1'b0), .out(multiplexer_1_out), .sel(or_2_out));
endmodule

// CU
module Control (
  input  Clock,
  input  [31:0] IR_In,
  input  Z_In,
  output IR_LD,
  output [7:0] T,
  output [3:0] D,
  output RAM_R_prime_W,
  output RAM_EN,
  output AR_LD,
  output PC_BUS,
  output PC_INC,
  output PC_LD,
  output DR_BUS,
  output DR_LD,
  output R_BUS,
  output R_LD,
  output ACC_BUS,
  output ACC_CLR,
  output ACC_LD,
  output [2:0] ALU_S,
  output OUTR_LD,
  output Z_LD
);

  wire n1bit_reg_1_data_out, s_ld_1_p5, sc_clr_1_p16;
  wire [15:0] s_ld_1_p3;

  // IR_LD ir_ld_1: pin names not known; wires that end beside it: T[2], Clock, IR_LD
  // RAM_RW ram_rw_1: pin names not known; wires that end beside it: T[1], T[3], T[5], s_ld_1_p3[1], s_ld_1_p3[2], s_ld_1_p3[5], s_ld_1_p3[6], Z_In, RAM_R_prime_W
  // RAM_EN ram_en_1: pin names not known; wires that end beside it: T[1], T[3], T[5], T[6], s_ld_1_p3[1], s_ld_1_p3[2], s_ld_1_p3[5], s_ld_1_p3[6], Z_In, RAM_EN
  // AR_LD ar_ld_1: pin names not known; wires that end beside it: T[0], T[2], T[4], Clock, s_ld_1_p3[1], s_ld_1_p3[2], AR_LD
  // PC_BUS pc_bus_1: pin names not known; wires that end beside it: T[0], T[2], PC_BUS
  // PC_INC pc_inc_1: pin names not known; wires that end beside it: T[1], T[3], Clock, s_ld_1_p3[1], s_ld_1_p3[2], s_ld_1_p3[6], Z_In, PC_INC
  // PC_LD pc_ld_1: pin names not known; wires that end beside it: T[4], Clock, s_ld_1_p3[5], s_ld_1_p3[6], Z_In, PC_LD
  // DR_BUS dr_bus_1: pin names not known; wires that end beside it: T[4], T[6], s_ld_1_p3[1], s_ld_1_p3[2], s_ld_1_p3[5], s_ld_1_p3[6], Z_In, DR_BUS
  // DR_LD dr_ld_1: pin names not known; wires that end beside it: T[1], T[3], T[5], Clock, s_ld_1_p3[1], s_ld_1_p3[2], s_ld_1_p3[5], s_ld_1_p3[6], Z_In, DR_LD
  // R_BUS r_bus_1: pin names not known; wires that end beside it: T[3], s_ld_1_p3[4], s_ld_1_p3[8], s_ld_1_p3[9], s_ld_1_p3[12], R_BUS
  // R_LD r_ld_1: pin names not known; wires that end beside it: s_ld_1_p3[13], T[3], Clock, s_ld_1_p3[3], R_LD
  // ACC_BUS acc_bus_1: pin names not known; wires that end beside it: T[3], T[5], s_ld_1_p3[2], s_ld_1_p3[3], s_ld_1_p3[7], ACC_BUS
  // ACC_CLR acc_clr_1: pin names not known; wires that end beside it: T[3], s_ld_1_p3[11], ACC_CLR
  // ACC_LD acc_ld_1: pin names not known; wires that end beside it: T[3], T[6], Clock, s_ld_1_p3[1], s_ld_1_p3[4], s_ld_1_p3[8], s_ld_1_p3[9], s_ld_1_p3[10], s_ld_1_p3[12], s_ld_1_p3[13], s_ld_1_p3[14], ACC_LD
  // ALU_SEL alu_sel_1: pin names not known; wires that end beside it: s_ld_1_p3[15], s_ld_1_p3[1], s_ld_1_p3[4], s_ld_1_p3[9], s_ld_1_p3[10], s_ld_1_p3[12], s_ld_1_p3[13], ALU_S[0], ALU_S[1], ALU_S[2]
  // OUTR_LD outr_ld_1: pin names not known; wires that end beside it: s_ld_1_p3[14], s_ld_1_p3[15], T[3], Clock, s_ld_1_p3[7], OUTR_LD
  // Z_LD z_ld_1: pin names not known; wires that end beside it: Z_LD
  // S_LD s_ld_1: pin names not known; wires that end beside it: T[3], Clock, s_ld_1_p3[0], T[4], s_ld_1_p5
  // SC_CLR sc_clr_1: pin names not known; wires that end beside it: s_ld_1_p3[9], s_ld_1_p3[10], s_ld_1_p3[11], s_ld_1_p3[12], s_ld_1_p3[13], s_ld_1_p3[14], s_ld_1_p3[15], Z_In, T[5], T[7], s_ld_1_p3[1], s_ld_1_p3[2], s_ld_1_p3[5], s_ld_1_p3[6], Z_In, sc_clr_1_p16
  Timer timer_1 (.T_Out(T), .Clock(Clock), .Stop(n1bit_reg_1_data_out), .Clear(sc_clr_1_p16));
  _1bit_reg u_1bit_reg_1 (.Data(1'b1), .Clock(Clock), .Load(s_ld_1_p5), .Clear(1'b0), .Data_out(n1bit_reg_1_data_out));
  Decoder decoder_1 (.D_Out(s_ld_1_p3), .Debug_Instruction(D), .IR_In(IR_In));
endmodule
